// Logisim project BigASM Ejercicio 62.circ as structural Verilog
module BOARD_BIG_ASM (
  output out_1
);

  wire button_1_out, CLK, CLR, d_ff_1_q, not_1_out, Write, Write_ASCII;
  wire [6:0] ASCII;
  wire [7:0] counter_1_q;
  wire [23:0] Dir_INPUT, Dir_MEMORY;
  wire [31:0] INPUT, MEMORY_IN, MEMORY_OUT;

  Button button_1 (.out(button_1_out));
  Clock clock_1 (.out(CLK));
  D_Flip_Flop d_ff_1 (.clk(CLK), .D(1'b1), .Q(d_ff_1_q), .reset(button_1_out));  // open: Qn, preset, en
  D_Flip_Flop d_ff_2 (.clk(CLK), .D(d_ff_1_q), .Qn(CLR), .reset(button_1_out));  // open: Q, preset, en
  BIG_ASM big_asm_1 (
    .DATA_INPUT(INPUT), .MEMORY_IN(MEMORY_OUT), .CLK(CLK), .CLR(CLR), .DIR_INPUT(Dir_INPUT),
    .MEMORY_OUT(MEMORY_IN), .DIR_MEMORY(Dir_MEMORY), .Write_OUTPUT(Write), .ASCII(ASCII),
    .Write_ASCII(Write_ASCII), .END(out_1));
  MEMORY memory_1 (.DIR(Dir_MEMORY), .DATA_IN(MEMORY_IN), .WRITE(Write), .CLK(CLK), .CLR(CLR), .DATA_OUT(MEMORY_OUT));
  INPUT input_1 (.DIR(Dir_INPUT), .CLK(CLK), .DATA_OUT(INPUT));
  Counter counter_1 (.load(1'b0), .count(not_1_out), .Q(counter_1_q), .clk(CLK), .clr(CLR));  // open: D, carry
  not not_1 (not_1_out, out_1);
  // Probe on counter_1_q
  TTY #(.rows(32), .cols(60)) tty_1 (.data(ASCII), .clk(CLK), .we(Write_ASCII), .clr(CLR));

  // Other names for the same wires on the sheet: END = out_1

  // Notes on the sheet:
  //   COUNTER
  //   BOARD
endmodule

module INPUT (
  input  [23:0] DIR,
  input  CLK,
  output [31:0] DATA_OUT
);

  RAM #(.addrWidth(24), .dataWidth(32)) ram_1 (.addr(DIR), .data(DATA_OUT), .clk(CLK), .ld(1'b1));  // open: sel, clr
endmodule

module MEMORY (
  input  [23:0] DIR,
  input  [31:0] DATA_IN,
  input  WRITE,
  input  CLK,
  input  CLR,
  output [31:0] DATA_OUT
);

  RAM #(.addrWidth(24), .dataWidth(32), .bus("separate")) ram_1 (
    .addr(DIR), .din(DATA_IN), .data(DATA_OUT), .str(WRITE), .clk(CLK), .clr(CLR));  // open: sel, ld
endmodule

module BIG_ASM (
  input  [31:0] DATA_INPUT,
  input  [31:0] MEMORY_IN,
  input  CLK,
  input  CLR,
  output [23:0] DIR_INPUT,
  output [31:0] MEMORY_OUT,
  output [23:0] DIR_MEMORY,
  output Write_OUTPUT,
  output [6:0] ASCII,
  output Write_ASCII,
  output END
);

  ASM_X asm_x_1 (
    .in_1(CLR), .in_2(CLK), .in_3(DATA_INPUT), .OUTPUT(END), .out_5(DIR_INPUT), .out_6(Write_ASCII),
    .out_7(ASCII));

  assign Write_OUTPUT = 1'b0;

  // Other names for the same wires on the sheet: DIR[23:0] = DIR_INPUT; MEMORY[31:0] = DATA_INPUT;
  //   W_ASCII = Write_ASCII
endmodule

module PRINT_UDEC (
  input  [31:0] num,
  input  start,
  input  CLK,
  input  RST,
  output [6:0] ASCII,
  output Write_ASCII,
  output \end 
);

  wire _0_c, _0_n, demultiplexer_1_out0, demultiplexer_2_out0, demultiplexer_2_out1, demultiplexer_3_out0,
       demultiplexer_3_out1, IDLE_2_q, IDLE_3_q, IDLE_4_q, IDLE_q, Lc, Lc_0, Ln, Ln_0, or_1_out;
  wire [23:0] bit_extender_1_out;
  wire [31:0] c, c___1, c___1_t, divider_1_rem, memory_1_data_out, multiplexer_1_out, multiplexer_2_out,
       multiplexer_3_out, n, n___10, n___10___48;

  Multiplexer #(.width(32), .enable("false")) multiplexer_1 (
    .in0(num), .in1(n___10), .out(multiplexer_1_out), .sel(Lc_0));
  Divider #(.width(32)) divider_1 (.a(n), .b(32'ha), .out(n___10), .rem(divider_1_rem));  // open: upper
  Adder #(.width(32)) adder_1 (.a(divider_1_rem), .b(32'h30), .out(n___10___48));  // open: cin, cout
  or or_1 (or_1_out, demultiplexer_1_out0, \end );
  Register #(.width(32)) u_n (.D(multiplexer_1_out), .en(Ln), .Q(n), .clk(CLK), .clr(RST));
  D_Flip_Flop IDLE (.clk(CLK), .D(or_1_out), .Q(IDLE_q), .preset(RST));  // open: Qn, en, reset
  Demultiplexer #(.enable("false")) demultiplexer_1 (
    .out0(demultiplexer_1_out0), .out1(Ln_0), .in(IDLE_q), .sel(start));
  or or_2 (Write_ASCII, demultiplexer_3_out0, demultiplexer_2_out1);
  Multiplexer #(.width(32), .enable("false")) multiplexer_2 (
    .in0(c___1), .in1(c___1_t), .out(multiplexer_2_out), .sel(Write_ASCII));
  Adder #(.width(32)) adder_2 (.a(c), .b(32'h1), .out(c___1));  // open: cin, cout
  Subtractor #(.width(32)) subtractor_1 (.a(c), .b(32'h1), .out(c___1_t));  // open: bin, bout
  D_Flip_Flop IDLE_2 (.clk(CLK), .D(Ln_0), .Q(IDLE_2_q), .reset(RST));  // open: Qn, preset, en
  Register #(.width(32)) u_c (.D(multiplexer_2_out), .en(Lc), .Q(c), .clk(CLK), .clr(RST));
  or or_3 (Lc_0, IDLE_2_q, demultiplexer_3_out1);
  Multiplexer #(.width(32), .enable("false")) multiplexer_3 (
    .in0(c), .in1(c___1_t), .out(multiplexer_3_out), .sel(Write_ASCII));
  Comparator #(.width(32), .mode("unsigned")) comparator_1 (.a({32{1'b0}}), .b(n), .lt(_0_n));  // open: gt, eq
  Comparator #(.width(32), .mode("unsigned")) comparator_2 (.a({32{1'b0}}), .b(c), .lt(_0_c));  // open: gt, eq
  D_Flip_Flop IDLE_3 (.clk(CLK), .D(Write_ASCII), .Q(IDLE_3_q), .reset(RST));  // open: Qn, preset, en
  Demultiplexer #(.enable("false")) demultiplexer_2 (
    .out0(demultiplexer_2_out0), .out1(demultiplexer_2_out1), .in(IDLE_3_q), .sel(_0_c));
  Bit_Extender #(.in_width(32), .out_width(24)) bit_extender_1 (.in(multiplexer_3_out), .out(bit_extender_1_out));
  D_Flip_Flop IDLE_4 (.clk(CLK), .D(Lc_0), .Q(IDLE_4_q), .reset(RST));  // open: Qn, preset, en
  or or_4 (Lc, Lc_0, Write_ASCII);
  or or_5 (Ln, Ln_0, Lc_0);
  Demultiplexer #(.enable("false")) demultiplexer_3 (
    .out0(demultiplexer_3_out0), .out1(demultiplexer_3_out1), .in(IDLE_4_q), .sel(_0_n));
  D_Flip_Flop IDLE_5 (.clk(CLK), .D(demultiplexer_2_out0), .Q(\end ), .reset(RST));  // open: Qn, preset, en
  MEMORY memory_1 (
    .DIR(bit_extender_1_out), .DATA_IN(n___10___48), .WRITE(Lc_0), .CLK(CLK), .CLR(RST),
    .DATA_OUT(memory_1_data_out));
  Bit_Extender #(.in_width(32), .out_width(7)) bit_extender_2 (.in(memory_1_data_out), .out(ASCII));

  // Other names for the same wires on the sheet: Lc_1 = Write_ASCII; Sc = Write_ASCII; Ln_1 = Lc_0; Sn = Lc_0;
  //   Write = Lc_0
endmodule

module PRINT_DEC (
  input  [31:0] num,
  input  start,
  input  CLK,
  input  RST,
  output [6:0] ASCII,
  output Write_ASCII,
  output END
);

  wire demultiplexer_1_out0, demultiplexer_1_out1, demultiplexer_2_out0, demultiplexer_3_out0, end_t,
       IDLE_3_q, IDLE_q, or_1_out, or_2_out, or_3_out, S_ASCII, startUDEC, Write_ASCII_1;
  wire [6:0] ASCII_t;
  wire [31:0] multiplexer_1_out, negator_1_out;

  or or_1 (or_1_out, demultiplexer_1_out0, END);
  Negator #(.width(32)) negator_1 (.in(num), .out(negator_1_out));
  D_Flip_Flop IDLE (.clk(CLK), .D(or_1_out), .Q(IDLE_q), .preset(RST));  // open: Qn, en, reset
  Demultiplexer #(.enable("false")) demultiplexer_1 (
    .out0(demultiplexer_1_out0), .out1(demultiplexer_1_out1), .in(IDLE_q), .sel(start));
  Multiplexer #(.width(32), .enable("false")) multiplexer_1 (
    .in0(num), .in1(negator_1_out), .out(multiplexer_1_out), .sel(num[31]));
  Demultiplexer #(.enable("false")) demultiplexer_2 (
    .out0(demultiplexer_2_out0), .out1(S_ASCII), .in(demultiplexer_1_out1), .sel(num[31]));
  or or_2 (or_2_out, demultiplexer_2_out0, S_ASCII);
  D_Flip_Flop IDLE_2 (.clk(CLK), .D(or_2_out), .Q(startUDEC), .reset(RST));  // open: Qn, preset, en
  PRINT_UDEC print_udec_1 (
    .num(multiplexer_1_out), .start(startUDEC), .CLK(CLK), .RST(RST), .ASCII(ASCII_t),
    .Write_ASCII(Write_ASCII_1), .\end (end_t));
  D_Flip_Flop IDLE_3 (.clk(CLK), .D(or_3_out), .Q(IDLE_3_q), .reset(RST));  // open: Qn, preset, en
  or or_3 (or_3_out, startUDEC, demultiplexer_3_out0);
  Demultiplexer #(.enable("false")) demultiplexer_3 (
    .out0(demultiplexer_3_out0), .out1(END), .in(IDLE_3_q), .sel(end_t));
  Multiplexer #(.width(7), .enable("false")) multiplexer_2 (
    .in0(ASCII_t), .in1(7'b0101101), .out(ASCII), .sel(S_ASCII));
  or or_4 (Write_ASCII, S_ASCII, Write_ASCII_1);

  // Other names for the same wires on the sheet: sign = num[31]; Write_ASCII_0 = S_ASCII
endmodule

module TEST_PRINT (
  input  [31:0] in_1,
  output out_2
);

  wire button_1_out, button_2_out, CLK, CLR, d_ff_1_q, Write_ASCII;
  wire [6:0] ASCII;

  Button button_1 (.out(button_1_out));
  Clock clock_1 (.out(CLK));
  D_Flip_Flop d_ff_1 (.clk(CLK), .D(1'b1), .Q(d_ff_1_q), .reset(button_1_out));  // open: Qn, preset, en
  D_Flip_Flop d_ff_2 (.clk(CLK), .D(d_ff_1_q), .Qn(CLR), .reset(button_1_out));  // open: Q, preset, en
  Button button_2 (.out(button_2_out));
  PRINT_UDEC print_udec_1 ();  // open: num, start, CLK, RST, ASCII, Write_ASCII, end
  PRINT_DEC print_dec_1 (
    .num(in_1), .start(button_2_out), .CLK(CLK), .RST(CLR), .ASCII(ASCII), .Write_ASCII(Write_ASCII),
    .END(out_2));
  TTY #(.rows(32), .cols(60)) tty_1 (.data(ASCII), .clk(CLK), .we(Write_ASCII), .clr(CLR));
endmodule

module Data_Path (
  input  in_1,
  input  in_2,
  input  in_3,
  input  [31:0] in_4,
  input  in_5,
  input  in_6,
  input  in_7,
  input  in_8,
  input  in_9,
  input  in_10,
  output out_11,
  output out_12,
  output [23:0] out_13,
  output out_14,
  output out_15,
  output out_16,
  output out_17
);

  wire I___N___1_t;
  wire [23:0] DIR___1, multiplexer_2_out;
  wire [31:0] I, I___1, L_I, multiplexer_1_out, N, N___1;

  Multiplexer #(.width(32), .enable("false")) multiplexer_1 (
    .in0(32'h1), .in1(I___1), .out(multiplexer_1_out), .sel(in_7));
  Register #(.width(32)) register_1 (.D(multiplexer_1_out), .en(in_3), .Q(I), .clk(in_9));  // open: clr
  Adder #(.width(32)) adder_1 (.a(I), .b(32'h1), .out(I___1));  // open: cin, cout
  Comparator #(.width(32)) comparator_1 (.a(I), .b(N___1), .lt(I___N___1_t));  // open: gt, eq
  Register #(.width(32)) register_2 (.D(in_4), .en(in_1), .Q(N), .clk(in_9));  // open: clr
  Comparator #(.width(32)) comparator_2 (.a(in_4), .b(L_I), .gt(out_16), .lt(out_17));  // open: eq
  Subtractor #(.width(32)) subtractor_1 (.a(N), .b(32'h1), .out(N___1));  // open: bin, bout
  Register #(.width(32)) register_3 (.D(in_4), .en(in_5), .Q(L_I), .clk(in_9));  // open: clr
  and and_1 (out_14, out_11, out_12);
  Multiplexer #(.width(24), .enable("false")) multiplexer_2 (
    .in0({24{1'b0}}), .in1(DIR___1), .out(multiplexer_2_out), .sel(in_10));
  Register #(.width(1)) register_4 (.D(1'b1), .en(in_2), .Q(out_11), .clk(in_9));  // open: clr
  Register #(.width(1)) register_5 (.D(1'b1), .en(in_6), .Q(out_12), .clk(in_9));  // open: clr
  Register #(.width(24)) register_6 (.D(multiplexer_2_out), .en(in_8), .Q(out_13), .clk(in_9));  // open: clr
  Adder #(.width(24)) adder_2 (.a(out_13), .b(24'h1), .out(DIR___1));  // open: cin, cout

  // Other names for the same wires on the sheet: C = out_11; C___D = out_14; Clock = in_9; D = out_12;
  //   DIR[23:0] = out_13; I___N___1 = out_15; L__I = in_5; L_C = in_2; L_D = in_6; L_DIR = in_8;
  //   L_I_1____L_I = out_17; L_I_1____L_I_t = out_16; L_I_t = in_3; L_N = in_1; MEMORY[31:0] = in_4; S_DIR = in_10;
  //   S_I = in_7

  // Notes on the sheet:
  //   DATA PATH
  //   INPUT
  //   OUTPUT
endmodule

module Control_Unit (
  input  in_1,
  input  in_2,
  input  in_3,
  input  in_4,
  input  in_5,
  input  in_6,
  output out_7,
  output out_8,
  output out_9,
  output out_10,
  output out_11,
  output out_12,
  output out_13,
  output out_14,
  output out_15
);

  wire AFTER_IF_q, demultiplexer_1_out0, demultiplexer_2_out0, demultiplexer_2_out1, demultiplexer_3_out0,
       demultiplexer_4_out0, demultiplexer_5_out0, demultiplexer_5_out1, IDLE_q, L__I__0, L__I__1, L_D1,
       or_1_out, or_5_out, or_8_out, WHILE_q;

  or or_1 (or_1_out, demultiplexer_1_out0, out_15);
  Demultiplexer #(.enable("false")) demultiplexer_1 (
    .out0(demultiplexer_1_out0), .out1(out_8), .in(IDLE_q), .sel(in_5));
  D_Flip_Flop IDLE (.clk(in_2), .D(or_1_out), .Q(IDLE_q), .preset(in_5));  // open: Qn, en, reset
  or or_2 (out_7, L__I__0, L_D1, out_14);
  D_Flip_Flop AFTER_size (.clk(in_2), .D(out_8), .Q(L__I__0));  // open: Qn, preset, en, reset
  or or_3 (out_9, L__I__0, L_D1, out_14);
  D_Flip_Flop d_ff_1 (.clk(in_2), .D(L__I__0), .Q(L_D1));  // open: Qn, preset, en, reset
  or or_4 (out_12, L_D1, out_14);
  or or_5 (or_5_out, L_D1, out_14);
  or or_6 (out_10, L__I__0, L__I__1);
  D_Flip_Flop WHILE (.clk(in_2), .D(or_5_out), .Q(WHILE_q));  // open: Qn, preset, en, reset
  Demultiplexer #(.enable("false")) demultiplexer_2 (
    .out0(demultiplexer_2_out0), .out1(demultiplexer_2_out1), .in(WHILE_q), .sel(in_1));
  Demultiplexer #(.enable("false")) demultiplexer_3 (
    .out0(demultiplexer_3_out0), .out1(out_11), .in(demultiplexer_2_out1), .sel(in_4));
  Demultiplexer #(.enable("false")) demultiplexer_4 (
    .out0(demultiplexer_4_out0), .out1(out_13), .in(demultiplexer_3_out0), .sel(in_3));
  or or_7 (L__I__1, demultiplexer_4_out0, out_13, out_11);
  Demultiplexer #(.enable("false")) demultiplexer_5 (
    .out0(demultiplexer_5_out0), .out1(demultiplexer_5_out1), .in(AFTER_IF_q), .sel(in_6));
  D_Flip_Flop AFTER_IF (.clk(in_2), .D(L__I__1), .Q(AFTER_IF_q));  // open: Qn, preset, en, reset
  or or_8 (or_8_out, demultiplexer_2_out0, demultiplexer_5_out1);
  D_Flip_Flop d_ff_2 (.clk(in_2), .D(demultiplexer_5_out0), .Q(out_14));  // open: Qn, preset, en, reset
  D_Flip_Flop END (.clk(in_2), .D(or_8_out), .Q(out_15));  // open: Qn, preset, en, reset

  // Other names for the same wires on the sheet: C___D = in_6; CLOCK = in_2; End = out_15; I___N___1 = in_1;
  //   L__I = out_10; L_C = out_11; L_d = out_13; L_DIR = out_7; L_I = out_12; L_I___1____L_i = in_3;
  //   L_I___1____L_i_t = in_4; L_n = out_8; L_D0 = L__I__0; S_D0 = L__I__0; L_I0 = L_D1; S_D1 = L_D1; S_DIR = out_9;
  //   L_D2 = out_14; L_I1 = out_14; S_D2 = out_14; S_I = out_14; Start = in_5

  // Notes on the sheet:
  //   INPUT
  //   CONTROL UNIT
  //   OUTPUT
endmodule

module SORTED (
  input  in_1,
  input  [31:0] in_2,
  input  in_3,
  output OUTPUT,
  output [23:0] out_5,
  output out_6,
  output out_7
);

  wire C___D, control_unit_1_out_7, control_unit_1_out_8, control_unit_1_out_9, control_unit_1_out_10,
       control_unit_1_out_11, control_unit_1_out_12, control_unit_1_out_13, control_unit_1_out_14, i___n___1,
       L_i___1____L_i, L_i___1____L_i_t;

  Control_Unit control_unit_1 (
    .out_8(control_unit_1_out_8), .out_10(control_unit_1_out_10), .in_1(i___n___1),
    .out_7(control_unit_1_out_7), .out_12(control_unit_1_out_12), .in_2(in_3), .out_9(control_unit_1_out_9),
    .in_4(L_i___1____L_i_t), .out_14(control_unit_1_out_14), .in_5(in_1), .out_15(OUTPUT),
    .out_11(control_unit_1_out_11), .out_13(control_unit_1_out_13), .in_3(L_i___1____L_i), .in_6(C___D));
  Data_Path data_path_1 (
    .in_4(in_2), .in_8(control_unit_1_out_7), .in_1(control_unit_1_out_8), .out_13(out_5), .out_11(out_6),
    .out_12(out_7), .out_14(C___D), .out_15(i___n___1), .in_10(control_unit_1_out_9),
    .in_5(control_unit_1_out_10), .out_16(L_i___1____L_i_t), .out_17(L_i___1____L_i), .in_9(in_3),
    .in_2(control_unit_1_out_11), .in_6(control_unit_1_out_13), .in_3(control_unit_1_out_12),
    .in_7(control_unit_1_out_14));

  // Other names for the same wires on the sheet: C = out_6; Clock = in_3; D = out_7; DIR[23:0] = out_5; END = OUTPUT;
  //   MEMORY[31:0] = in_2; START = in_1

  // Notes on the sheet:
  //   INPUT
endmodule

module ASM_X (
  input  in_1,
  input  in_2,
  input  [31:0] in_3,
  output OUTPUT,
  output [23:0] out_5,
  output out_6,
  output [6:0] out_7
);

  wire d_ff_1_q, demultiplexer_1_out0, demultiplexer_1_out1, demultiplexer_2_out0, demultiplexer_2_out1, END,
       or_1_out, or_2_out, print_1_out_8, sorted_1_out_6, sorted_1_out_7;

  or or_1 (or_1_out, demultiplexer_1_out0, demultiplexer_2_out1);
  D_Flip_Flop d_ff_1 (.clk(in_2), .D(or_1_out), .Q(d_ff_1_q), .preset(in_1));  // open: Qn, en, reset
  Demultiplexer #(.enable("false")) demultiplexer_1 (
    .out0(demultiplexer_1_out0), .out1(demultiplexer_1_out1), .in(d_ff_1_q), .sel(in_1));
  SORTED sorted_1 (
    .in_3(in_2), .in_1(demultiplexer_1_out1), .OUTPUT(END), .out_5(out_5), .in_2(in_3),
    .out_6(sorted_1_out_6), .out_7(sorted_1_out_7));
  PRINT_2 print_1 (
    .INPUT(in_2), .in_2(in_1), .out_8(print_1_out_8), .in_3(END), .in_4(sorted_1_out_6),
    .in_5(sorted_1_out_7), .OUTPUT(out_7), .out_7(out_6));
  or or_2 (or_2_out, print_1_out_8, demultiplexer_2_out0);
  D_Flip_Flop d_ff_2 (.clk(in_2), .D(or_2_out), .Q(OUTPUT));  // open: Qn, preset, en, reset
  Demultiplexer #(.enable("false")) demultiplexer_2 (
    .out0(demultiplexer_2_out0), .out1(demultiplexer_2_out1), .in(OUTPUT), .sel(in_1));

  // Other names for the same wires on the sheet: ASCII[6:0] = out_7; Clock = in_2; DIR[23:0] = out_5; End_t = OUTPUT;
  //   MEMORY[31:0] = in_3; Start = in_1; Write_ASCII = out_6

  // Notes on the sheet:
  //   INPUT
  //   ASM
endmodule

module PRINT_2 (
  input  INPUT,
  input  in_2,
  input  in_3,
  input  in_4,
  input  in_5,
  output [6:0] OUTPUT,
  output out_7,
  output out_8
);

  wire demultiplexer_1_out0, IDLE_q, or_1_out;
  wire [6:0] multiplexer_1_out;

  or or_1 (or_1_out, demultiplexer_1_out0, out_8);
  D_Flip_Flop IDLE (.clk(INPUT), .D(or_1_out), .Q(IDLE_q), .preset(in_3), .reset(in_2));  // open: Qn, en
  Demultiplexer #(.enable("false")) demultiplexer_1 (
    .out0(demultiplexer_1_out0), .out1(out_7), .in(IDLE_q), .sel(in_3));
  Multiplexer #(.select(2), .width(7), .enable("false")) multiplexer_1 (
    .in0(7'b1000011), .in1(7'b1000011), .in2(7'b1000100), .in3(7'b1001110), .out(multiplexer_1_out),
    .sel({in_5, in_4}));
  Register #(.width(7)) register_1 (.D(multiplexer_1_out), .en(out_7), .Q(OUTPUT), .clk(INPUT), .clr(in_2));
  D_Flip_Flop END (.clk(INPUT), .D(out_7), .Q(out_8), .reset(in_2));  // open: Qn, preset, en

  // Other names for the same wires on the sheet: ASCII[6:0] = OUTPUT; CLOCK = INPUT; End = out_8; RST = in_2;
  //   C = in_4; S[1:0] = {in_5, in_4}; D = in_5; Start = in_3; L_A = out_7; Write_ASCII = out_7

  // Notes on the sheet:
  //   CONTROL UNIT
  //   PRINT
  //   DATA PATH
endmodule
